// Logisim project RegFile.circ as structural Verilog: 2 circuits, main circuit main
module main (
  input  [15:0] WriteData0,
  input  [15:0] WriteData1,
  input  [2:0] WriteSelect0,
  input  [2:0] ReadSelect0,
  input  [2:0] ReadSelect1,
  input  WE0,
  input  WE1,
  input  Clock,
  output [15:0] Reg0,
  output [15:0] Reg1,
  output [15:0] Reg2,
  output [15:0] Reg3,
  output [15:0] Reg4,
  output [15:0] Reg5,
  output [15:0] Reg6,
  output [15:0] Reg7,
  output [15:0] ReadData0,
  output [15:0] ReadData1
);

  wire demultiplexer_1_out0, demultiplexer_1_out1, demultiplexer_1_out2, demultiplexer_1_out3,
       demultiplexer_1_out4, demultiplexer_1_out5, demultiplexer_1_out6, demultiplexer_1_out7,
       demultiplexer_2_out0, demultiplexer_2_out1, demultiplexer_2_out2, demultiplexer_2_out3,
       demultiplexer_2_out4, demultiplexer_2_out5, demultiplexer_2_out6, demultiplexer_2_out7, or_1_p3,
       or_2_p3, or_3_p3, or_4_p3, or_5_p3, or_6_out, or_7_out, or_8_out;
  wire [2:0] adder_1_out;
  wire [15:0] multiplexer_1_out, multiplexer_2_out, multiplexer_3_out, multiplexer_4_out, multiplexer_5_out,
       multiplexer_6_out, multiplexer_7_out, multiplexer_8_out;

  Adder #(.width(3)) adder_1 (.a(WriteSelect0), .b(3'b001), .out(adder_1_out));  // open: cin, cout
  Multiplexer #(.select(3), .width(16)) multiplexer_1 (
    .in0(WriteData1), .in1(WriteData0), .in2(WriteData0), .in3(WriteData0), .in4(WriteData0),
    .in5(WriteData0), .in6(WriteData0), .in7(WriteData0), .out(multiplexer_1_out), .sel(adder_1_out));  // open: en
  Multiplexer #(.select(3), .width(16)) multiplexer_2 (
    .in0(WriteData0), .in1(WriteData1), .in2(WriteData0), .in3(WriteData0), .in4(WriteData0),
    .in5(WriteData0), .in6(WriteData0), .in7(WriteData0), .out(multiplexer_2_out), .sel(adder_1_out));  // open: en
  Multiplexer #(.select(3), .width(16)) multiplexer_3 (
    .in0(WriteData0), .in1(WriteData0), .in2(WriteData1), .in3(WriteData0), .in4(WriteData0),
    .in5(WriteData0), .in6(WriteData0), .in7(WriteData0), .out(multiplexer_3_out), .sel(adder_1_out));  // open: en
  Multiplexer #(.select(3), .width(16)) multiplexer_4 (
    .in0(WriteData0), .in1(WriteData0), .in2(WriteData0), .in3(WriteData1), .in4(WriteData0),
    .in5(WriteData0), .in6(WriteData0), .in7(WriteData0), .out(multiplexer_4_out), .sel(adder_1_out));  // open: en
  Multiplexer #(.select(3), .width(16)) multiplexer_5 (
    .in0(WriteData0), .in1(WriteData0), .in2(WriteData0), .in3(WriteData0), .in4(WriteData1),
    .in5(WriteData0), .in6(WriteData0), .in7(WriteData0), .out(multiplexer_5_out), .sel(adder_1_out));  // open: en
  Multiplexer #(.select(3), .width(16)) multiplexer_6 (
    .in0(WriteData0), .in1(WriteData0), .in2(WriteData0), .in3(WriteData0), .in4(WriteData0),
    .in5(WriteData1), .in6(WriteData0), .in7(WriteData0), .out(multiplexer_6_out), .sel(adder_1_out));  // open: en
  Multiplexer #(.select(3), .width(16)) multiplexer_7 (
    .in0(WriteData0), .in1(WriteData0), .in2(WriteData0), .in3(WriteData0), .in4(WriteData0),
    .in5(WriteData0), .in6(WriteData1), .in7(WriteData0), .out(multiplexer_7_out), .sel(adder_1_out));  // open: en
  Multiplexer #(.select(3), .width(16)) multiplexer_8 (
    .in0(WriteData0), .in1(WriteData0), .in2(WriteData0), .in3(WriteData0), .in4(WriteData0),
    .in5(WriteData0), .in6(WriteData0), .in7(WriteData1), .out(multiplexer_8_out), .sel(adder_1_out));  // open: en
  Demultiplexer #(.select(3)) demultiplexer_1 (
    .out0(demultiplexer_1_out0), .out1(demultiplexer_1_out1), .out2(demultiplexer_1_out2),
    .out3(demultiplexer_1_out3), .out4(demultiplexer_1_out4), .out5(demultiplexer_1_out5),
    .out6(demultiplexer_1_out6), .out7(demultiplexer_1_out7), .in(WE1), .sel(adder_1_out));  // open: en
  Demultiplexer #(.select(3)) demultiplexer_2 (
    .out0(demultiplexer_2_out0), .out1(demultiplexer_2_out1), .out2(demultiplexer_2_out2),
    .out3(demultiplexer_2_out3), .out4(demultiplexer_2_out4), .out5(demultiplexer_2_out5),
    .out6(demultiplexer_2_out6), .out7(demultiplexer_2_out7), .in(WE0), .sel(WriteSelect0));  // open: en
  Register #(.width(16)) register_1 (.D(multiplexer_1_out), .en(or_1_p3), .Q(Reg0), .clk(Clock));  // open: clr
  // OR_Gate or_1: pin names not known; wires that end beside it: demultiplexer_1_out0, demultiplexer_2_out0, or_1_p3
  Register #(.width(16)) register_2 (.D(multiplexer_2_out), .en(or_2_p3), .Q(Reg1), .clk(Clock));  // open: clr
  // OR_Gate or_2: pin names not known; wires that end beside it: demultiplexer_1_out1, demultiplexer_2_out1, or_2_p3
  Register #(.width(16)) register_3 (.D(multiplexer_3_out), .en(or_3_p3), .Q(Reg2), .clk(Clock));  // open: clr
  // OR_Gate or_3: pin names not known; wires that end beside it: demultiplexer_1_out2, demultiplexer_2_out2, or_3_p3
  Register #(.width(16)) register_4 (.D(multiplexer_4_out), .en(or_4_p3), .Q(Reg3), .clk(Clock));  // open: clr
  // OR_Gate or_4: pin names not known; wires that end beside it: demultiplexer_1_out3, demultiplexer_2_out3, or_4_p3
  Register #(.width(16)) register_5 (.D(multiplexer_5_out), .en(or_5_p3), .Q(Reg4), .clk(Clock));  // open: clr
  // OR_Gate or_5: pin names not known; wires that end beside it: demultiplexer_1_out4, demultiplexer_2_out4, or_5_p3
  Register #(.width(16)) register_6 (.D(multiplexer_6_out), .en(or_6_out), .Q(Reg5), .clk(Clock));  // open: clr
  or or_6 (or_6_out, demultiplexer_1_out5, demultiplexer_2_out5);
  Register #(.width(16)) register_7 (.D(multiplexer_7_out), .en(or_7_out), .Q(Reg6), .clk(Clock));  // open: clr
  or or_7 (or_7_out, demultiplexer_1_out6, demultiplexer_2_out6);
  Register #(.width(16)) register_8 (.D(multiplexer_8_out), .en(or_8_out), .Q(Reg7), .clk(Clock));  // open: clr
  or or_8 (or_8_out, demultiplexer_1_out7, demultiplexer_2_out7);
  Multiplexer #(.select(3), .width(16)) multiplexer_9 (
    .in0(Reg0), .in1(Reg1), .in2(Reg2), .in3(Reg3), .in4(Reg4), .in5(Reg5), .in6(Reg6), .in7(Reg7),
    .out(ReadData0), .sel(ReadSelect0));  // open: en
  Multiplexer #(.select(3), .width(16)) multiplexer_10 (
    .in0(Reg0), .in1(Reg1), .in2(Reg2), .in3(Reg3), .in4(Reg4), .in5(Reg5), .in6(Reg6), .in7(Reg7),
    .out(ReadData1), .sel(ReadSelect1));  // open: en

  // Other names for the same wires on the sheet: WriteEnable0 = WE0; WriteEnable1 = WE1

  // Notes on the sheet:
  //   Inputs
  //   Add the registers to this file
  //   These can be used for debug and testing
  //   WriteSelect0 - Register to write to
  //   ReadSelect0 - First register to read data from
  //   ReadSelect1 - Second register to read data from
  //   WE0 - Enable writing to 1 register
  //   WE1 - Enable writing to 2nd register (mul/div)
  //   ReadData0 - Data being read from first register
  //   ReadData1 - Data being read from second register
  //   WriteData0 - The data to be written to register by most instructions
  //   WriteData1 - The data to be written to second register by mul/div
  //    Don't modify any of the inputs/outputs in this file!
  //   and design the logic to control them
  //   Outputs
endmodule

module test (
  input  [15:0] Write_data_A,
  input  Write_Enable_Port_A,
  input  [2:0] in_3,
  input  [15:0] Write_data_B,
  input  Write_Enable_Port_B,
  input  [2:0] Select_Read_A,
  input  [2:0] Select_Read_B
);

  wire Clock_out;
  wire [15:0] main_1_readdata0, main_1_readdata1, main_1_reg0, main_1_reg1, main_1_reg2, main_1_reg3,
       main_1_reg4, main_1_reg5, main_1_reg6, main_1_reg7;

  // Probe on main_1_reg1
  // Probe on main_1_reg0
  // Probe on main_1_reg3
  // Probe on main_1_reg2
  Button Clock (.out(Clock_out));
  // Probe on main_1_reg4
  // Probe on main_1_reg5
  // Probe on main_1_reg7
  // Probe on main_1_reg6
  main main_1 (
    .WriteData0(Write_data_A), .WriteData1(Write_data_B), .ReadData0(main_1_readdata0),
    .ReadData1(main_1_readdata1), .WriteSelect0(in_3), .ReadSelect0(Select_Read_A),
    .ReadSelect1(Select_Read_B), .Reg0(main_1_reg0), .Reg1(main_1_reg1), .Reg2(main_1_reg2),
    .Reg3(main_1_reg3), .Reg4(main_1_reg4), .Reg5(main_1_reg5), .Reg6(main_1_reg6), .Reg7(main_1_reg7),
    .WE0(Write_Enable_Port_A), .WE1(Write_Enable_Port_B), .Clock(Clock_out));
  // Probe on main_1_readdata0
  // Probe on main_1_readdata1

  // Notes on the sheet:
  //   Test your circuit!
endmodule
