// Logisim project umips.circ as structural Verilog: 3 circuits, main circuit main
module main (
  output [15:0] Reg0,
  output [15:0] Reg1,
  output [15:0] Reg2,
  output [15:0] Reg3,
  output [15:0] Reg4,
  output [15:0] Reg5,
  output [15:0] Reg6,
  output [15:0] Reg7,
  output [3:0] Output3,
  output [3:0] Output2,
  output [3:0] Output1,
  output [3:0] Output0,
  output halt
);

  wire and_1_out, and_2_out, and_3_out, and_4_out, branching, clock, GT, immUse, j, jal, jr, liUse, LT,
       MemLoad, MemWrite, not_1_out, not_2_out, or_1_out, or_2_out, put, Subop, WE0, WE1, Z;
  wire [1:0] Bop;
  wire [2:0] ALUOp, rs, rt;
  wire [3:0] Opcode;
  wire [7:0] adder_1_out, adder_2_out, adder_3_out, adder_4_out, adder_5_out, intImm, multiplexer_1_out,
       multiplexer_2_out, multiplexer_3_out, multiplexer_4_out, multiplexer_5_out, multiplexer_6_out,
       multiplexer_7_out, pc;
  wire [15:0] ALUa, ALUb, bit_extender_1_out, imm, MemLoadWrite, multiplexer_8_out, multiplexer_9_out,
       multiplexer_10_out, multiplexer_11_out, rom_1_data, WriteDATAa, WriteDATAb;

  Multiplexer #(.width(8)) multiplexer_1 (
    .in0(multiplexer_7_out), .in1(intImm), .out(multiplexer_1_out), .sel(or_1_out));  // open: en
  // NOT_Gate not_1 has open pins: in=open, out=not_1_out
  or or_1 (or_1_out, j, jal);
  Control control_1 (
    .Opcode(Opcode), .Subop(Subop), .ALUOp(ALUOp), .ImmediateUse(immUse), .WriteEnable0(WE0),
    .WriteEnable1(WE1), .liUse(liUse), .MemWrite(MemWrite), .MemLoad(MemLoad), .halt(halt), .put(put),
    .intImm(intImm), .imm(imm), .Bop(Bop), .branching(branching), .j(j), .jr(jr), .jal(jal));
  Adder adder_1 (.a(8'h1), .b(pc), .out(adder_1_out));  // open: cin, cout
  Adder adder_2 (.a(8'h1), .b(pc), .out(adder_2_out));  // open: cin, cout
  Adder adder_3 (.a(8'h1), .b(pc), .out(adder_3_out));  // open: cin, cout
  Adder adder_4 (.a(8'h1), .b(pc), .out(adder_4_out));  // open: cin, cout
  Register register_1 (.D(multiplexer_1_out), .en(not_1_out), .Q(pc), .clk(clock));  // open: clr
  Multiplexer #(.width(8)) multiplexer_2 (
    .in0(adder_1_out), .in1(intImm), .out(multiplexer_2_out), .sel(and_1_out));  // open: en
  and and_1 (and_1_out, branching, GT);
  Multiplexer #(.width(8)) multiplexer_3 (
    .in0(adder_2_out), .in1(intImm), .out(multiplexer_3_out), .sel(and_2_out));  // open: en
  and and_2 (and_2_out, branching, LT);
  Multiplexer #(.width(8)) multiplexer_4 (
    .in0(adder_3_out), .in1(intImm), .out(multiplexer_4_out), .sel(and_3_out));  // open: en
  and and_3 (and_3_out, branching, not_2_out);
  not not_2 (not_2_out, Z);
  Multiplexer #(.width(8)) multiplexer_5 (
    .in0(adder_4_out), .in1(intImm), .out(multiplexer_5_out), .sel(and_4_out));  // open: en
  and and_4 (and_4_out, branching, Z);
  LED led_1 (.in(halt));
  InstructionDecode instructiondecode_1 (
    .Instruction(rom_1_data), .Subop(Subop), .rt(rt), .rs(rs), .Opcode(Opcode), .Immediate(intImm));
  ROM #(.dataWidth(16)) rom_1 (.addr(pc), .data(rom_1_data), .sel(1'b1));
  Multiplexer #(.select(2), .width(8)) multiplexer_6 (
    .in0(multiplexer_2_out), .in1(multiplexer_3_out), .in2(multiplexer_4_out), .in3(multiplexer_5_out),
    .out(multiplexer_6_out), .sel(Bop));  // open: en
  Multiplexer #(.width(8)) multiplexer_7 (
    .in0(multiplexer_6_out), .in1(ALUa[7:0]), .out(multiplexer_7_out), .sel(jr));  // open: en
  Clock clock_1 (.out(clock));
  Multiplexer #(.width(16)) multiplexer_8 (
    .in0(WriteDATAa), .in1(imm), .out(multiplexer_8_out), .sel(liUse));  // open: en
  Multiplexer #(.width(16)) multiplexer_9 (
    .in0(multiplexer_8_out), .in1(MemLoadWrite), .out(multiplexer_9_out), .sel(MemLoad));  // open: en
  Adder adder_5 (.a(8'h1), .b(pc), .out(adder_5_out));  // open: cin, cout
  assign bit_extender_1_out = {{8{1'b0}}, adder_5_out};  // Bit_Extender bit_extender_1
  Multiplexer #(.width(16)) multiplexer_10 (
    .in0(multiplexer_9_out), .in1(bit_extender_1_out), .out(multiplexer_10_out), .sel(jal));  // open: en
  Hex_Digit_Display hex_digit_display_1 (.value(Output3));  // open: dp
  Register #(.width(16)) register_2 (
    .D(ALUa), .en(put), .Q({Output3, Output2, Output1, Output0}), .clk(clock));  // open: clr
  ALU_main main_1 (
    .ALUOp(ALUOp), .A(ALUa), .B(multiplexer_11_out), .Result(WriteDATAa), .GT(GT), .Zero(Z), .LT(LT),
    .Result2(WriteDATAb));  // open: in_4
  Multiplexer #(.width(16)) multiplexer_11 (.in0(ALUb), .in1(imm), .out(multiplexer_11_out), .sel(immUse));  // open: en
  Hex_Digit_Display hex_digit_display_2 (.value(Output2));  // open: dp
  Hex_Digit_Display hex_digit_display_3 (.value(Output1));  // open: dp
  or or_2 (or_2_out, MemWrite, MemLoad);
  Hex_Digit_Display hex_digit_display_4 (.value(Output0));  // open: dp
  RAM #(.dataWidth(16), .bus("separate")) ram_1 (
    .addr(ALUb[7:0]), .din(ALUa), .data(MemLoadWrite), .str(MemWrite), .sel(or_2_out), .clk(clock),
    .ld(MemLoad));  // open: clr
  RegFile_main main_2 (
    .WriteData0(multiplexer_10_out), .WriteData1(WriteDATAb), .ReadData0(ALUa), .ReadData1(ALUb),
    .WriteSelect0(rs), .ReadSelect0(rs), .ReadSelect1(rt), .Reg0(Reg0), .Reg1(Reg1), .Reg2(Reg2),
    .Reg3(Reg3), .Reg4(Reg4), .Reg5(Reg5), .Reg6(Reg6), .Reg7(Reg7), .WE0(WE0), .WE1(WE1), .Clock(clock));

  // Notes on the sheet:
  //   Control
  //   contents of rom_1 (hex, n*v repeats v):
  //   111
  //   Design your CPU in this file
  //    Don't modify these, they are used for debug and testing
  //   You must connect Reg0..7 to the top ports of the register file.
  //   Include everything here (ALU, RegFile, Control, PC, RAM, ROM, LEDs, Displays, ...)
  //   Connect Output3..0 to your LED display.
  //   Output3 is the most significant
  //   Connect halt to your halt LED
endmodule

module InstructionDecode (
  input  [15:0] Instruction,
  output Subop,
  output [2:0] rt,
  output [2:0] rs,
  output [3:0] Opcode,
  output [7:0] Immediate
);


  assign Immediate = Instruction[8:1];
  assign Opcode = Instruction[15:12];
  assign rs = Instruction[11:9];
  assign rt = Instruction[8:6];
  assign Subop = Instruction[0];
endmodule

module Control (
  input  [3:0] Opcode,
  input  Subop,
  input  [7:0] intImm,
  output [15:0] imm,
  output [1:0] Bop,
  output [2:0] ALUOp,
  output branching,
  output ImmediateUse,
  output j,
  output jr,
  output jal,
  output WriteEnable0,
  output WriteEnable1,
  output liUse,
  output MemWrite,
  output MemLoad,
  output halt,
  output put
);

  wire add, addi, addui, \and , bn, bp, bx, bz, decoder_1_out0, decoder_1_out4, decoder_1_out6,
       decoder_1_out8, decoder_1_out12, decoder_1_out14, div, mul, \nor , or_1_out, sllv, srlv, sub;
  wire [15:0] bit_extender_1_out, bit_extender_2_out;

  Decoder #(.select(4)) decoder_1 (
    .out0(decoder_1_out0), .out1(put), .out2(bp), .out3(bn), .out4(decoder_1_out4), .out5(jal),
    .out6(decoder_1_out6), .out7(jr), .out8(decoder_1_out8), .out9(halt), .out10(liUse), .out11(bx),
    .out12(decoder_1_out12), .out13(j), .out14(decoder_1_out14), .out15(bz), .sel(Opcode));  // open: en
  or or_1 (or_1_out, addui, add, addi);
  Demultiplexer demultiplexer_1 (.out0(add), .out1(sub), .in(decoder_1_out0), .sel(Subop));  // open: en
  Demultiplexer demultiplexer_2 (.out0(mul), .out1(div), .in(decoder_1_out4), .sel(Subop));  // open: en
  Demultiplexer demultiplexer_3 (.out0(MemWrite), .out1(MemLoad), .in(decoder_1_out14), .sel(Subop));  // open: en
  Demultiplexer demultiplexer_4 (.out0(srlv), .out1(sllv), .in(decoder_1_out6), .sel(Subop));  // open: en
  Demultiplexer demultiplexer_5 (.out0(addui), .out1(addi), .in(decoder_1_out12), .sel(Subop));  // open: en
  Priority_Encoder priority_encoder_1 (
    .in0(1'b1), .in1(\nor ), .in2(or_1_out), .in3(sub), .in4(mul), .in5(div), .in6(sllv), .in7(srlv),
    .out(ALUOp));  // open: en_in, gs, en_out
  or or_2 (ImmediateUse, addui, addi, liUse, bp, bn, bx, bz, jal, j);
  or or_3 (WriteEnable0, add, sub, \and , \nor , addui, addi, div, mul, sllv, srlv, MemLoad, liUse, jal);
  or or_4 (WriteEnable1, div, mul);
  Demultiplexer demultiplexer_6 (.out0(\nor ), .out1(\and ), .in(decoder_1_out8), .sel(Subop));  // open: en
  assign bit_extender_1_out = {{8{1'b0}}, intImm};  // Bit_Extender bit_extender_1
  assign bit_extender_2_out = {{8{intImm[7]}}, intImm};  // Bit_Extender bit_extender_2
  Priority_Encoder #(.select(2)) priority_encoder_2 (
    .in0(1'b1), .in1(bn), .in2(bx), .in3(bz), .out(Bop));  // open: gs, en_out, en_in
  or or_5 (branching, bp, bn, bx, bz);
  Multiplexer #(.width(16)) multiplexer_1 (
    .in0(bit_extender_1_out), .in1(bit_extender_2_out), .out(imm), .sel(addi));  // open: en

  // Other names for the same wires on the sheet: li = liUse; lw = MemLoad; sw = MemWrite
endmodule
